// Logisim project PONG.circ as structural Verilog: 6 circuits, main circuit Players
module main (
);

  wire cl, clock_1_out, clock_2_out, placar_1_ponto, placar_2_ponto;
  wire [3:0] pt1, pt2;
  wire [4:0] bol_y, \bolinha_horizontal_1_saída ;
  wire [6:0] keyboard_1_data;
  wire [29:0] demultiplexer_1_out0, demultiplexer_1_out1, demultiplexer_1_out2, demultiplexer_1_out3,
       demultiplexer_1_out4, demultiplexer_1_out5, demultiplexer_1_out6, demultiplexer_1_out7,
       demultiplexer_1_out8, demultiplexer_1_out9, demultiplexer_1_out10, demultiplexer_1_out11,
       demultiplexer_1_out12, demultiplexer_1_out13, demultiplexer_1_out14, demultiplexer_1_out15,
       demultiplexer_1_out16, demultiplexer_1_out17, demultiplexer_1_out18, demultiplexer_1_out19,
       demultiplexer_1_out20, demultiplexer_1_out21, demultiplexer_1_out22, demultiplexer_1_out23,
       demultiplexer_1_out24, demultiplexer_1_out25, demultiplexer_1_out26, demultiplexer_1_out27,
       demultiplexer_1_out28, demultiplexer_1_out29, demultiplexer_1_out30, demultiplexer_1_out31,
       demultiplexer_2_out29, or_1_out, or_2_out, p1, p2;

  Contador contador_1 (.Ponto(placar_2_ponto), .Clear(cl), .\saída (pt1));
  Contador contador_2 (.Ponto(placar_1_ponto), .Clear(cl), .\saída (pt2));
  Placar placar_1 (
    .player(p2), .pos_x(\bolinha_horizontal_1_saída ), .ponto(placar_1_ponto), .bolinha_Y(bol_y),
    .cte({5{1'b1}}));
  Placar placar_2 (
    .player(p1), .pos_x(\bolinha_horizontal_1_saída ), .ponto(placar_2_ponto), .bolinha_Y(bol_y),
    .cte({5{1'b0}}));
  Clock clock_1 (.out(clock_1_out));
  Keyboard #(.buflen(1)) keyboard_1 (.clk(clock_1_out), .data(keyboard_1_data));  // open: re, clr, avail
  Hex_Digit_Display hex_digit_display_1 (.value(pt1));  // open: dp
  Button Reset (.out(cl));
  Players players_1 (.Clock(clock_1_out), .Teclado(keyboard_1_data), .\Saída__P1 (p1), .\Saída__P2 (p2));
  Hex_Digit_Display hex_digit_display_2 (.value(pt2));  // open: dp
  bolinha_horizontal bolinha_horizontal_1 (.clock(clock_2_out), .\saída (\bolinha_horizontal_1_saída ));
  DotMatrix #(.matrixcols(32), .matrixrows(30)) dotmatrix_1 (
    .col0(or_1_out), .col1(demultiplexer_1_out1), .col2(demultiplexer_1_out2), .col3(demultiplexer_1_out3),
    .col4(demultiplexer_1_out4), .col5(demultiplexer_1_out5), .col6(demultiplexer_1_out6),
    .col7(demultiplexer_1_out7), .col8(demultiplexer_1_out8), .col9(demultiplexer_1_out9),
    .col10(demultiplexer_1_out10), .col11(demultiplexer_1_out11), .col12(demultiplexer_1_out12),
    .col13(demultiplexer_1_out13), .col14(demultiplexer_1_out14), .col15(demultiplexer_1_out15),
    .col16(demultiplexer_1_out16), .col17(demultiplexer_1_out17), .col18(demultiplexer_1_out18),
    .col19(demultiplexer_1_out19), .col20(demultiplexer_1_out20), .col21(demultiplexer_1_out21),
    .col22(demultiplexer_1_out22), .col23(demultiplexer_1_out23), .col24(demultiplexer_1_out24),
    .col25(demultiplexer_1_out25), .col26(demultiplexer_1_out26), .col27(demultiplexer_1_out27),
    .col28(demultiplexer_1_out28), .col29(demultiplexer_1_out29), .col30(demultiplexer_1_out30),
    .col31(or_2_out));
  assign or_1_out = p1 | demultiplexer_1_out0;  // OR_Gate or_1, 30 bits wide
  Bolinha_vertical bolinha_vertical_1 (.clock(clock_2_out), .\saída (bol_y));
  Clock #(.highDuration(50), .lowDuration(50)) clock_2 (.out(clock_2_out));
  Demultiplexer #(.select(5), .width(30)) demultiplexer_1 (
    .out0(demultiplexer_1_out0), .out1(demultiplexer_1_out1), .out2(demultiplexer_1_out2),
    .out3(demultiplexer_1_out3), .out4(demultiplexer_1_out4), .out5(demultiplexer_1_out5),
    .out6(demultiplexer_1_out6), .out7(demultiplexer_1_out7), .out8(demultiplexer_1_out8),
    .out9(demultiplexer_1_out9), .out10(demultiplexer_1_out10), .out11(demultiplexer_1_out11),
    .out12(demultiplexer_1_out12), .out13(demultiplexer_1_out13), .out14(demultiplexer_1_out14),
    .out15(demultiplexer_1_out15), .out16(demultiplexer_1_out16), .out17(demultiplexer_1_out17),
    .out18(demultiplexer_1_out18), .out19(demultiplexer_1_out19), .out20(demultiplexer_1_out20),
    .out21(demultiplexer_1_out21), .out22(demultiplexer_1_out22), .out23(demultiplexer_1_out23),
    .out24(demultiplexer_1_out24), .out25(demultiplexer_1_out25), .out26(demultiplexer_1_out26),
    .out27(demultiplexer_1_out27), .out28(demultiplexer_1_out28), .out29(demultiplexer_1_out29),
    .out30(demultiplexer_1_out30), .out31(demultiplexer_1_out31), .in(demultiplexer_2_out29),
    .sel(\bolinha_horizontal_1_saída ));  // open: en
  Demultiplexer #(.select(5)) demultiplexer_2 (
    .out0(demultiplexer_2_out29[29]), .out1(demultiplexer_2_out29[28]), .out2(demultiplexer_2_out29[27]),
    .out3(demultiplexer_2_out29[26]), .out4(demultiplexer_2_out29[25]), .out5(demultiplexer_2_out29[24]),
    .out6(demultiplexer_2_out29[23]), .out7(demultiplexer_2_out29[22]), .out8(demultiplexer_2_out29[21]),
    .out9(demultiplexer_2_out29[20]), .out10(demultiplexer_2_out29[19]), .out11(demultiplexer_2_out29[18]),
    .out12(demultiplexer_2_out29[17]), .out13(demultiplexer_2_out29[16]), .out14(demultiplexer_2_out29[15]),
    .out15(demultiplexer_2_out29[14]), .out16(demultiplexer_2_out29[13]), .out17(demultiplexer_2_out29[12]),
    .out18(demultiplexer_2_out29[11]), .out19(demultiplexer_2_out29[10]), .out20(demultiplexer_2_out29[9]),
    .out21(demultiplexer_2_out29[8]), .out22(demultiplexer_2_out29[7]), .out23(demultiplexer_2_out29[6]),
    .out24(demultiplexer_2_out29[5]), .out25(demultiplexer_2_out29[4]), .out26(demultiplexer_2_out29[3]),
    .out27(demultiplexer_2_out29[2]), .out28(demultiplexer_2_out29[1]), .out29(demultiplexer_2_out29[0]),
    .in(1'b1), .sel(bol_y));  // open: out30, out31, en
  assign or_2_out = demultiplexer_1_out31 | p2;  // OR_Gate or_2, 30 bits wide

  // Notes on the sheet:
  //   Player 2
  //   Teclado
  //   Para começar o jogo aperte ctrl+K
  //   Player 1
  //   PONG
  //   Horizontal
  //   Vertical
endmodule

module Players (
  input  Clock,
  input  [6:0] Teclado,
  output [29:0] \Saída__P1 ,
  output [29:0] \Saída__P2 
);

  wire comparator_1_eq, comparator_2_eq, comparator_3_eq, comparator_4_eq, or_1_out, or_2_out;
  wire [4:0] counter_1_q, counter_2_q;

  // Probe on 7'b1100001
  // Probe on 7'b1110001
  // Probe on 7'b0110011
  // Probe on 7'b0110110
  Comparator #(.width(7)) comparator_1 (.a(Teclado), .b(7'b0110011), .eq(comparator_1_eq));  // open: gt, lt
  Comparator #(.width(7)) comparator_2 (.a(Teclado), .b(7'b0110110), .eq(comparator_2_eq));  // open: gt, lt
  or or_1 (or_1_out, comparator_3_eq, comparator_4_eq);
  Comparator #(.width(7), .mode("unsigned")) comparator_3 (
    .a(Teclado), .b(7'b1110001), .eq(comparator_3_eq));  // open: gt, lt
  or or_2 (or_2_out, comparator_2_eq, comparator_1_eq);
  Comparator #(.width(7), .mode("unsigned")) comparator_4 (
    .a(Teclado), .b(7'b1100001), .eq(comparator_4_eq));  // open: gt, lt
  Counter #(.width(5), .max('h19), .ongoal("stay")) counter_1 (
    .load(comparator_1_eq), .count(or_2_out), .Q(counter_1_q), .clk(Clock));  // open: D, carry, clr
  Counter #(.width(5), .max('h19), .ongoal("stay")) counter_2 (
    .load(comparator_4_eq), .count(or_1_out), .Q(counter_2_q), .clk(Clock));  // open: D, carry, clr
  Shifter #(.width(30)) shifter_1 (.in(30'h1f), .\dist (counter_2_q), .out(\Saída__P1 ));
  Shifter #(.width(30)) shifter_2 (.in(30'h1f), .\dist (counter_1_q), .out(\Saída__P2 ));

  // Notes on the sheet:
  //   Q = 1110 001
  //   A = 1100 001
  //   6 = 0110 110
  //   3 = 0110 011
endmodule

module Contador (
  input  Ponto,
  input  Clear,
  output [3:0] \saída 
);

  wire and_1_out, or_1_out, t_ff_1_qn, t_ff_2_qn, t_ff_3_qn;

  T_Flip_Flop t_ff_1 (.clk(Ponto), .T(1'b1), .Q(\saída [0]), .Qn(t_ff_1_qn), .reset(or_1_out));  // open: preset, en
  T_Flip_Flop t_ff_2 (.clk(t_ff_1_qn), .T(1'b1), .Q(\saída [1]), .Qn(t_ff_2_qn), .reset(or_1_out));  // open: preset, en
  T_Flip_Flop t_ff_3 (.clk(t_ff_2_qn), .T(1'b1), .Q(\saída [2]), .Qn(t_ff_3_qn), .reset(or_1_out));  // open: preset, en
  T_Flip_Flop t_ff_4 (.clk(t_ff_3_qn), .T(1'b1), .Q(\saída [3]), .reset(or_1_out));  // open: Qn, preset, en
  and and_1 (and_1_out, \saída [3], \saída [1]);
  or or_1 (or_1_out, and_1_out, Clear);
endmodule

module Bolinha_vertical (
  input  clock,
  output [4:0] \saída 
);

  wire comparator_1_eq, comparator_2_eq, or_1_out, t_ff_1_qn;

  Comparator #(.width(5)) comparator_1 (.a(\saída ), .b({5{1'b0}}), .eq(comparator_1_eq));  // open: gt, lt
  Comparator #(.width(5)) comparator_2 (.a(\saída ), .b(5'b11101), .eq(comparator_2_eq));  // open: gt, lt
  or or_1 (or_1_out, comparator_1_eq, comparator_2_eq);
  T_Flip_Flop t_ff_1 (.clk(or_1_out), .T(or_1_out), .Qn(t_ff_1_qn));  // open: Q, preset, reset, en
  Counter #(.width(5), .max('h1d)) counter_1 (
    .load(t_ff_1_qn), .Q(\saída ), .clk(clock));  // open: D, count, carry, clr
endmodule

module bolinha_horizontal (
  input  clock,
  output [4:0] \saída 
);

  wire comparator_1_eq, comparator_2_eq, or_1_out, t_ff_1_qn;

  Comparator #(.width(5)) comparator_1 (.a(\saída ), .b({5{1'b0}}), .eq(comparator_1_eq));  // open: gt, lt
  Comparator #(.width(5)) comparator_2 (.a(\saída ), .b({5{1'b1}}), .eq(comparator_2_eq));  // open: gt, lt
  or or_1 (or_1_out, comparator_1_eq, comparator_2_eq);
  T_Flip_Flop t_ff_1 (.clk(or_1_out), .T(or_1_out), .Qn(t_ff_1_qn));  // open: Q, preset, reset, en
  Counter #(.width(5), .max('h1f)) counter_1 (
    .load(t_ff_1_qn), .Q(\saída ), .clk(clock));  // open: D, count, carry, clr
endmodule

module Placar (
  input  [4:0] pos_x,
  input  [4:0] cte,
  input  [29:0] player,
  input  [4:0] bolinha_Y,
  output ponto
);

  wire comparator_1_eq, multiplexer_1_out, not_1_out;

  Multiplexer #(.select(5)) multiplexer_1 (
    .in0(player[29]), .in1(player[28]), .in2(player[27]), .in3(player[26]), .in4(player[25]),
    .in5(player[24]), .in6(player[23]), .in7(player[22]), .in8(player[21]), .in9(player[20]),
    .in10(player[19]), .in11(player[18]), .in12(player[17]), .in13(player[16]), .in14(player[15]),
    .in15(player[14]), .in16(player[13]), .in17(player[12]), .in18(player[11]), .in19(player[10]),
    .in20(player[9]), .in21(player[8]), .in22(player[7]), .in23(player[6]), .in24(player[5]),
    .in25(player[4]), .in26(player[3]), .in27(player[2]), .in28(player[1]), .in29(player[0]),
    .out(multiplexer_1_out), .sel(bolinha_Y));  // open: in30, in31, en
  not not_1 (not_1_out, multiplexer_1_out);
  Comparator #(.width(5)) comparator_1 (.a(pos_x), .b(cte), .eq(comparator_1_eq));  // open: gt, lt
  and and_1 (ponto, not_1_out, comparator_1_eq);
endmodule
